# Fritzing sketch motorspeed (saved by Fritzing 0.9.3b)
breadboards: 1

parts:
  Q1 = NPN-Transistor [package="TO92 [THT]"]
  D1 = Rectifier Diode [part_number=1N4001 package="300 mil [THT]"]
  UNO = Arduino Uno (Rev3)
  VCC1 = Battery block 9V
  R1 = Resistor [tolerance=±5% resistance=1k package=THT]
  R2 = Rotary Potentiometer (Large) [maximum_resistance=100k package=THT]
  M1 = DC Motor

nets:
  N1: Q1.E, UNO.GND, VCC1.-, R2.leg1
  N2: Q1.B, R1.Pin_1
  N3: Q1.C, D1.anode, M1.pin_2
  N4: D1.cathode, VCC1.+, M1.pin_1
  N5: UNO.A0, R2.wiper
  N6: UNO.D3_PWM, R1.Pin_0
  N7: UNO.5V, R2.leg2

// code stored in the sketch: motorspeed.ino
/*
 * motorspeed
 * 
 * A simple sketch to help demonstrate the used of an
 * NPN transistor and flyback diode to drive a motor
 * with its speed mapped to a potentiometer.
 * 
 * By Phillip Stearns for PGTE_5585_F2019
 * 
 */

#define POT_PIN A0
#define PWM_PIN 3

void setup() {
  pinMode(PWM_PIN, OUTPUT);
}

void loop() {
  // look ma, no variables!
  analogWrite(PWM_PIN, int(255 * analogRead(POT_PIN) / 1023.0));
  delay(20);
}
