# Fritzing sketch transistor_indicator (saved by Fritzing 0.9.3b)
breadboards: 1

parts:
  Q1 = NPN-Transistor [package="TO92 [THT]"]
  R1 = Resistor [tolerance=±5% resistance=1k package=THT]
  R2 = Resistor [tolerance=±5% resistance=470 package=THT]
  LED1 = LED - 5mm [color="Red (633nm)" package="5 mm [THT]"]
  TP1 = TEST-POINT [package=pad.02x.02]

nets:
  GND: Q1.E
  N1: Q1.B, R1.Pin_1
  N2: Q1.C, R2.Pin_0
  N3: R1.Pin_0, TP1.1
  N4: R2.Pin_1, LED1.cathode
  5V: LED1.anode
