# Fritzing sketch arduino2arduino (saved by Fritzing 0.9.3b)

parts:
  Part1 = Arduino Uno (Rev3)
  Part2 = Arduino Uno (Rev3)

nets:
  N1: Part1.D0/RX, Part2.D1/TX
  N2: Part1.D1/TX, Part2.D0/RX
  5V: Part1.5V, Part2.5V
  GND: Part1.GND, Part2.GND
